// Logisim project RPScirc.circ as structural Verilog: 2 circuits, main circuit main
module main (
  input  [2:0] P1,
  input  [2:0] P2,
  output Win,
  output p2Win,
  output tie
);
endmodule

module rps (
  input  R1,
  input  P1,
  input  S1,
  input  R2,
  input  P2,
  input  S2,
  output P1wins,
  output p2wins,
  output tie,
  output misinput
);

  wire and_1_out, and_2_out, and_3_out, and_4_out, and_5_out, and_6_out, and_7_out, and_8_out, and_9_out,
       and_10_out, and_11_out, and_12_out, and_13_out, and_14_out, and_15_out, and_16_out, and_17_out,
       and_18_out, and_19_out, not_1_out, not_2_out, not_3_out, not_4_out, not_5_out, not_6_out, not_7_out,
       not_8_out, not_9_out, not_10_out, not_11_out, not_12_out, not_13_out, not_14_out, not_15_out,
       not_16_out, not_17_out, not_18_out, not_19_out, not_20_out, not_21_out, not_22_out, not_23_out,
       not_24_out, not_25_out, not_26_out, not_27_out, not_28_out, not_29_out, not_30_out, not_31_out,
       not_32_out, not_33_out, not_34_out, not_35_out, not_36_out, not_37_out, not_38_out, not_39_out,
       not_40_out, not_41_out, not_42_out, not_43_out, not_44_out, not_45_out, not_46_out, not_47_out,
       not_48_out;

  not not_1 (not_1_out, R1);
  not not_2 (not_2_out, S1);
  not not_3 (not_3_out, P2);
  not not_4 (not_4_out, S2);
  not not_5 (not_5_out, P1);
  not not_6 (not_6_out, S1);
  not not_7 (not_7_out, R2);
  not not_8 (not_8_out, P2);
  not not_9 (not_9_out, R1);
  not not_10 (not_10_out, P1);
  not not_11 (not_11_out, R2);
  not not_12 (not_12_out, S2);
  not not_13 (not_13_out, R1);
  not not_14 (not_14_out, P1);
  not not_15 (not_15_out, P2);
  not not_16 (not_16_out, S2);
  not not_17 (not_17_out, R1);
  not not_18 (not_18_out, P1);
  not not_19 (not_19_out, R1);
  not not_20 (not_20_out, S1);
  not not_21 (not_21_out, R2);
  not not_22 (not_22_out, P2);
  not not_23 (not_23_out, P1);
  not not_24 (not_24_out, S1);
  not not_25 (not_25_out, R2);
  not not_26 (not_26_out, S2);
  not not_27 (not_27_out, R1);
  not not_28 (not_28_out, P1);
  not not_29 (not_29_out, R2);
  not not_30 (not_30_out, P2);
  not not_31 (not_31_out, R1);
  not not_32 (not_32_out, S1);
  not not_33 (not_33_out, R2);
  not not_34 (not_34_out, S2);
  not not_35 (not_35_out, P1);
  not not_36 (not_36_out, S1);
  not not_37 (not_37_out, P2);
  not not_38 (not_38_out, S2);
  not not_39 (not_39_out, R1);
  not not_40 (not_40_out, P1);
  not not_41 (not_41_out, S1);
  not not_42 (not_42_out, R2);
  not not_43 (not_43_out, P2);
  not not_44 (not_44_out, S2);
  not not_45 (not_45_out, R2);
  not not_46 (not_46_out, P2);
  not not_47 (not_47_out, S1);
  not not_48 (not_48_out, S2);
  and and_1 (and_1_out, not_1_out, P1, not_2_out, R2, not_3_out, not_4_out);
  and and_2 (and_2_out, R1, not_5_out, not_6_out, not_7_out, not_8_out, S2);
  and and_3 (and_3_out, not_9_out, not_10_out, S1, not_11_out, P2, not_12_out);
  and and_4 (and_4_out, not_13_out, not_14_out, S1, R2, not_15_out, not_16_out);
  and and_5 (and_5_out, not_17_out, not_18_out, S1, R2, P2, S2);
  and and_6 (and_6_out, not_19_out, P1, not_20_out, not_21_out, not_22_out, S2);
  and and_7 (and_7_out, R1, not_23_out, not_24_out, not_25_out, P2, not_26_out);
  and and_8 (and_8_out, not_27_out, not_28_out, S1, not_29_out, not_30_out, S2);
  and and_9 (and_9_out, not_31_out, P1, not_32_out, not_33_out, P2, not_34_out);
  and and_10 (and_10_out, R1, not_35_out, not_36_out, R2, not_37_out, not_38_out);
  and and_11 (and_11_out, not_39_out, not_40_out, not_41_out);
  and and_12 (and_12_out, not_42_out, not_43_out, not_44_out);
  and and_13 (and_13_out, not_45_out, P2, S2);
  and and_14 (and_14_out, R2, not_46_out, S2);
  and and_15 (and_15_out, not_47_out, R2, P2);
  and and_16 (and_16_out, R2, P2, not_48_out);
  and and_17 (and_17_out, P1, S1);
  and and_18 (and_18_out, R1, S1);
  and and_19 (and_19_out, R1, P1);
  or or_1 (P1wins, and_1_out, and_2_out);
  or or_2 (p2wins, and_3_out, and_4_out, and_5_out, and_6_out, and_7_out);
  or or_3 (tie, and_8_out, and_9_out, and_10_out);
  or or_4 (misinput, and_11_out, and_12_out, and_13_out, and_14_out, and_15_out, and_16_out, and_17_out, and_18_out, and_19_out);
endmodule
